# Fritzing sketch arduinorc.1.1a_with_Sw1 (saved by Fritzing 0.7.10b)
breadboards: 1

parts:
  POT6 = Rotary Potentiometer (Small) [maximum_resistance=10kΩ]
  POT5 = Rotary Potentiometer (Small) [maximum_resistance=10kΩ]
  POT4 = Rotary Potentiometer (Small) [maximum_resistance=10kΩ]
  POT3 = Rotary Potentiometer (Small) [maximum_resistance=10kΩ]
  POT2 = Rotary Potentiometer (Small) [maximum_resistance=10kΩ]
  POT1 = Rotary Potentiometer (Small) [maximum_resistance=10kΩ]
  U1 = Voltage Regulator - 5V [package="TO220 [THT]"]
  SwArduino = Pushbutton [package=THT]
  SwMain = Pushbutton [package=THT]
  VCC = Battery block 9V
  SwTest = Pushbutton [package=THT]
  SwMode = Pushbutton [package=THT]
  SwThrottle = Pushbutton [package=THT]
  SwRate = Pushbutton [package=THT]
  ConnectRF = screw terminal, 4 pins
  SwBind = Pushbutton [package=THT]
  R1 = Resistor [tolerance=±5% resistance=12k package=THT]
  R2 = Resistor [tolerance=±5% resistance=10k package=THT]
  R3 = Resistor [tolerance=±5% resistance=270 package=THT]
  Nano1 = Arduino Nano v3.0
  LED1 = LED - 5mm [color="Red (633nm)" package="5 mm [THT]"]
  C2 = Ceramic Capacitor [capacitance=330nF voltage=10V package="200 mil [THT, multilayer]"]
  C1 = Ceramic Capacitor [capacitance=100nF voltage=10V package="200 mil [THT, multilayer]"]
  Sw1 = Pushbutton [package=THT]

nets:
  GND: POT6.leg1, POT5.leg1, POT4.leg1, POT3.leg1, POT2.leg1, POT1.leg1, U1.GND, VCC.-, SwTest.leg0, SwMode.leg0, SwThrottle.leg0, SwRate.leg0, ConnectRF.pin4, SwBind.leg0, R2.Pin_0, R3.Pin_1, Nano1.GND, C2.0, C1.0, Sw1.leg0
  N1: POT6.wiper, Nano1.A5
  N2: POT6.leg2, POT5.leg2, POT4.leg2, POT3.leg2, POT2.leg2, POT1.leg2, SwArduino.leg1, Nano1.+5V
  N3: POT5.wiper, Nano1.A4
  N4: POT4.wiper, Nano1.A3
  N5: POT3.wiper, Nano1.A2
  N6: POT2.wiper, Nano1.A1
  N7: POT1.wiper, Nano1.A0
  N8: U1.input_voltage, SwMain.leg0, C2.1
  N9: U1.output_voltage, SwArduino.leg0, ConnectRF.pin3, C1.1
  N10: SwMain.leg1, VCC.+
  N11: SwTest.leg1, Nano1.D8
  N12: SwMode.leg1, Nano1.D9
  N13: SwThrottle.leg1, Nano1.D11
  N14: SwRate.leg1, Nano1.D12
  N15: ConnectRF.pin1, R1.Pin_1, R2.Pin_1
  N16: ConnectRF.pin2, SwBind.leg1
  N17: R1.Pin_0, Nano1.D10
  N18: R3.Pin_0, LED1.cathode
  N19: Nano1.D2, Sw1.leg1
  N20: Nano1.D13, LED1.anode

notes:
  Gnd
  +5v
  Bind
  PPM
  Arduino Radio Control
  6 channels RC transmitter
  http://www.reseau.org/arduinorc
  10 Dec 2012 - version 1.1
  Arduino Radio Control - 6 channels RC transmitter
  10 Dec 2012 - v 1.1a - http://www.reseau.org/arduinorc
