# Fritzing sketch arduinorc.1.1b_stripboard (saved by Fritzing 0.7.11b)
stripboards: 1

parts:
  Nano1 = Arduino Nano v3.0
  JBatt = Screw terminal - 2 pins [package=THT]
  U1 = Voltage Regulator - 5V [package="TO220 [THT]"]
  C1 = Ceramic Capacitor [capacitance=100nF package="100 mil [THT, multilayer]"]
  C2 = Ceramic Capacitor [capacitance=100nF package="100 mil [THT, multilayer]"]
  S2 = Toggle Switch [package=THT]
  R1 = Resistor [tolerance=±5% resistance=270 package=THT]
  LED1 = LED - 5mm [color="Red (633nm)" package="5 mm [THT]"]
  JSWArduino = female pin header, 2 pins [form="♀ (female)"]
  JPot = female pin header, 6 pins [form="♀ (female)"]
  R2 = Resistor [tolerance=±5% resistance=10k package=THT]
  R3 = Resistor [tolerance=±5% resistance=12k package=THT]
  J5v = female pin header, 1 pin [form="♀ (female)"]
  JMode = female pin header, 1 pin [form="♀ (female)"]
  JPPM = female pin header, 1 pin [form="♀ (female)"]
  JModel = female pin header, 1 pin [form="♀ (female)"]
  JThrottle = female pin header, 1 pin [form="♀ (female)"]
  JRate = female pin header, 1 pin [form="♀ (female)"]
  JSw1 = female pin header, 1 pin [form="♀ (female)"]

nets:
  GND: Nano1.GND, JBatt.pin2, U1.GND, U1.output_voltage, C1.1, C2.0, C2.1, S2.COM, LED1.cathode, JSWArduino.pin1, R2.Pin_0, J5v.pin1
  N1: Nano1.D2, JSw1.pin1
  N2: Nano1.D8, JModel.pin1
  N3: Nano1.D9, JMode.pin1
  N4: Nano1.D10, R3.Pin_1
  N5: Nano1.D11, JThrottle.pin1
  N6: Nano1.D12, JRate.pin1
  N7: Nano1.D13, R1.Pin_0
  N8: Nano1.A0, JPot.pin6
  N9: Nano1.A1, JPot.pin5
  N10: Nano1.A2, JPot.pin4
  N11: Nano1.A3, JPot.pin3
  N12: Nano1.A4, JPot.pin2
  N13: Nano1.A5, JPot.pin1
  N14: Nano1.+5V, S2.L2, JSWArduino.pin2
  N15: JBatt.pin1, U1.input_voltage, C1.0
  N16: R1.Pin_1, LED1.anode
  N17: R2.Pin_1, R3.Pin_0, JPPM.pin1
