# Fritzing sketch 7805 regulator wiring (saved by Fritzing 0.8.0b)
breadboards: 1

parts:
  U1 = Voltage Regulator - 5V [package="TO220 [THT]"]
  C2 = Tantalum Capacitor [capacitance=100nF package="200 mil [THT, tantalum]"]
  C1 = Tantalum Capacitor [capacitance=0.33µF package="200 mil [THT, tantalum]"]
  VCC1 = Battery block 9V
  S1 = Pushbutton [package=THT]

nets:
  N1: U1.input_voltage, C1.+, S1.leg0
  N2: U1.GND, C2.-, C1.-, VCC1.-
  N3: U1.output_voltage, C2.+
  N4: VCC1.+, S1.leg1
